// Digital circuit DLlab2_03_01.dig as structural Verilog
module DLlab2_03_01 (
  input  A,
  input  B,
  input  Cin,
  output Cout,
  output Sum
);

  wire A_t, and_1_out, and_2_out, and_3_out, and_4_out, and_5_out, and_6_out, and_7_out, B_t, C;

  not not_1 (A_t, A);
  not not_2 (B_t, B);
  not not_3 (C, Cin);
  and and_1 (and_1_out, B, Cin);
  and and_2 (and_2_out, A, Cin);
  and and_3 (and_3_out, A, B);
  and and_4 (and_4_out, A_t, B_t, Cin);
  and and_5 (and_5_out, A, B_t, C);
  and and_6 (and_6_out, A_t, B, C);
  and and_7 (and_7_out, A, B, Cin);
  or or_1 (Cout, and_1_out, and_2_out, and_3_out);
  or or_2 (Sum, and_4_out, and_5_out, and_6_out, and_7_out);

  // Other names for the same wires on the sheet: C_t = Cin
endmodule
