// Digital circuit DLlab2_04_01.dig as structural Verilog
module DLlab2_04_01 (
  input  A,
  input  B,
  input  Cin,
  output Cout,
  output Sum
);

  wire A_t, B_t, C, or_1_out, or_2_out, or_3_out, or_4_out, or_5_out, or_6_out, or_7_out;

  not not_1 (A_t, A);
  not not_2 (B_t, B);
  not not_3 (C, Cin);
  or or_1 (or_1_out, A, B);
  or or_2 (or_2_out, B, Cin);
  or or_3 (or_3_out, A, Cin);
  or or_4 (or_4_out, A, B, Cin);
  or or_5 (or_5_out, A, B_t, C);
  or or_6 (or_6_out, A_t, B, C);
  or or_7 (or_7_out, A_t, B_t, Cin);
  and and_1 (Cout, or_1_out, or_2_out, or_3_out);
  and and_2 (Sum, or_4_out, or_5_out, or_6_out, or_7_out);

  // Other names for the same wires on the sheet: C_t = Cin
endmodule
