// Digital circuit DLlab2_05.dig as structural Verilog
module DLlab2_05 (
  input  A,
  input  B,
  input  C,
  input  D,
  input  clk,
  input  clk_2,
  input  clk_3,
  input  clk_4,
  output Z1,
  output Z2,
  output Z3
);

  wire A_eq_C_step1, A_t, and_3_out, and_4_out, and_5_out, and_6_out, and_7_out, and_8_out, and_9_out,
       and_10_out, and_11_out, and_12_out, B_t, C_t, D_t, z11, z21;

  and and_1 (z11, A, C_t);
  and and_2 (z21, A_t, C);
  and and_3 (and_3_out, A, C);
  and and_4 (and_4_out, A_t, C_t);
  or or_1 (A_eq_C_step1, and_3_out, and_4_out);
  not not_1 (A_t, A);
  not not_2 (B_t, B);
  not not_3 (C_t, C);
  not not_4 (D_t, D);
  Seven_Seg_Hex seven_seg_hex_1 (.d({clk_4, clk_3, A, B}), .dp(clk_4));
  and and_5 (and_5_out, B, D_t);
  and and_6 (and_6_out, B_t, D);
  and and_7 (and_7_out, B, D);
  and and_8 (and_8_out, B_t, D_t);
  Seven_Seg_Hex seven_seg_hex_2 (.d({clk_2, clk, C, D}), .dp(clk_2));
  and and_9 (and_9_out, A_eq_C_step1, and_5_out);
  and and_10 (and_10_out, A_eq_C_step1, and_6_out);
  and and_11 (and_11_out, A_eq_C_step1, and_7_out);
  and and_12 (and_12_out, A_eq_C_step1, and_8_out);
  or or_2 (Z1, z11, and_9_out);
  or or_3 (Z2, z21, and_10_out);
  or or_4 (Z3, and_11_out, and_12_out);
  // also tied to GND on the sheet: {clk_2, clk_4}
endmodule
