// Digital circuit DLlab2_06.dig as structural Verilog
module DLlab2_06 (
  input  A,
  input  B,
  input  C,
  input  D,
  input  clk,
  input  clk_2,
  input  clk_3,
  input  clk_4,
  output Z1,
  output Z2,
  output Z3
);

  wire A_t, B_t, C_t, D_t, or_1_out, or_2_out, or_3_out, or_4_out, or_5_out, or_6_out, or_7_out, or_8_out,
       or_9_out, or_10_out, or_11_out, or_12_out, or_13_out, or_14_out, or_15_out, or_16_out, or_17_out,
       or_18_out, or_19_out, or_20_out, or_21_out, or_22_out, or_23_out, or_24_out, or_25_out, or_26_out,
       or_27_out, or_28_out, or_29_out, or_30_out, or_31_out, or_32_out;

  or or_1 (or_1_out, A_t, B_t, C_t, D);
  or or_2 (or_2_out, A_t, B, C_t, D_t);
  or or_3 (or_3_out, A_t, B_t, C, D_t);
  or or_4 (or_4_out, A_t, B_t, C, D);
  or or_5 (or_5_out, A_t, B, C, D_t);
  or or_6 (or_6_out, A_t, B, C, D);
  or or_7 (or_7_out, A, B_t, C_t, D_t);
  or or_8 (or_8_out, A, B_t, C_t, D);
  or or_9 (or_9_out, A, B, C_t, D_t);
  or or_10 (or_10_out, A, B, C_t, D);
  or or_11 (or_11_out, A, B_t, C, D);
  or or_12 (or_12_out, A, B, C, D_t);
  and and_1 (Z3, or_1_out, or_2_out, or_3_out, or_4_out, or_5_out, or_6_out, or_7_out, or_8_out, or_9_out, or_10_out, or_11_out, or_12_out);
  or or_13 (or_13_out, A_t, B_t, C_t, D_t);
  or or_14 (or_14_out, A_t, B, C_t, D_t);
  or or_15 (or_15_out, A_t, B, C_t, D);
  or or_16 (or_16_out, A, B_t, C_t, D_t);
  or or_17 (or_17_out, A, B_t, C_t, D);
  or or_18 (or_18_out, A, B, C_t, D_t);
  or or_19 (or_19_out, A, B, C_t, D);
  or or_20 (or_20_out, A, B_t, C, D_t);
  or or_21 (or_21_out, A, B, C, D_t);
  or or_22 (or_22_out, A, B, C, D);
  and and_2 (Z1, or_13_out, or_14_out, or_15_out, or_16_out, or_17_out, or_18_out, or_19_out, or_20_out, or_21_out, or_22_out);
  or or_23 (or_23_out, A_t, B_t, C_t, D_t);
  or or_24 (or_24_out, A_t, B_t, C_t, D);
  or or_25 (or_25_out, A_t, B_t, C, D_t);
  or or_26 (or_26_out, A_t, B_t, C, D);
  or or_27 (or_27_out, A_t, B, C, D_t);
  or or_28 (or_28_out, A_t, B, C, D);
  or or_29 (or_29_out, A, B_t, C, D);
  or or_30 (or_30_out, A_t, B, C_t, D);
  or or_31 (or_31_out, A, B_t, C, D_t);
  or or_32 (or_32_out, A, B, C, D);
  and and_3 (Z2, or_23_out, or_24_out, or_25_out, or_26_out, or_27_out, or_28_out, or_29_out, or_30_out, or_31_out, or_32_out);
  not not_1 (A_t, A);
  not not_2 (B_t, B);
  not not_3 (C_t, C);
  not not_4 (D_t, D);
  Seven_Seg_Hex seven_seg_hex_1 (.d({clk_4, clk_3, A, B}), .dp(clk_4));
  Seven_Seg_Hex seven_seg_hex_2 (.d({clk_2, clk, C, D}), .dp(clk_2));
  // also tied to GND on the sheet: {clk_2, clk_4}
endmodule
