// Digital circuit DLlab2_06_01.dig as structural Verilog
module DLlab2_06_01 (
  input  A,
  input  B,
  input  C,
  input  D,
  output Z1,
  output Z2,
  output Z3
);

  wire and_1_out, and_2_out, and_3_out, not_1_out, not_2_out, not_3_out, not_4_out, or_1_out, or_2_out,
       or_3_out, or_4_out, or_5_out, or_6_out, or_7_out, or_8_out, or_9_out, or_10_out;

  not not_1 (not_1_out, A);
  not not_2 (not_2_out, B);
  not not_3 (not_3_out, C);
  not not_4 (not_4_out, D);
  or or_1 (or_1_out, not_3_out, A);
  and and_1 (and_1_out, or_7_out, or_3_out, or_1_out);
  not not_5 (Z2, and_1_out);
  or or_2 (or_2_out, C, not_1_out);
  and and_2 (and_2_out, or_8_out, or_4_out, or_2_out);
  not not_6 (Z1, and_2_out);
  or or_3 (or_3_out, not_4_out, B, C, A);
  or or_4 (or_4_out, D, not_2_out, C, A);
  or or_5 (or_5_out, not_4_out, not_2_out, C, A);
  or or_6 (or_6_out, D, B, C, A);
  or or_7 (or_7_out, not_4_out, B, not_3_out, not_1_out);
  not not_7 (Z3, and_3_out);
  or or_8 (or_8_out, D, not_2_out, not_3_out, not_1_out);
  and and_3 (and_3_out, or_10_out, or_9_out, or_6_out, or_5_out);
  or or_9 (or_9_out, not_4_out, not_2_out, not_3_out, not_1_out);
  or or_10 (or_10_out, D, B, not_3_out, not_1_out);
endmodule
